// Logisim project Boba Vending Machine.circ as structural Verilog: 1 circuit, main circuit main
module main (
  input  _1,
  input  _5,
  input  _10,
  input  _25,
  input  _50,
  input  _1_2,
  input  _5_2,
  input  _10_2,
  input  _20,
  input  in_10,
  output Total,
  output OverFlow
);
endmodule
